# Fritzing sketch ATTinyTimer (saved by Fritzing 0.9.3b)
stripboards: 1
breadboards: 1

parts:
  U1 = attiny85 [package=dip]
  Q1 = Basic FET N-Channel [package="TO220 [THT]"]
  R1 = Resistor [tolerance=±5% resistance=1k package=THT]
  R3 = Vertical Resistor [tolerance=±5% resistance=10k package=THT]
  S1 = Momentary Switch [package=ksa_sealed_tac_switch]
  Part1 = Arduino Nano (Rev3.0)
  VCC1 = Battery
  S2 = Pushbutton [package="[THT]"]
  S3 = Pushbutton [package="[THT]"]
  S4 = Pushbutton [package="[THT]"]
  SP1 = SPEAKER [package=pcb_mount_speaker]
  R4 = Resistor [tolerance=±5% resistance=1k package=THT]
  Grove1 = Grove OLED 128x96

nets:
  N1: U1.Pin_1, R3.Pin_1, S1.1
  N2: U1.Pin_4, Q1.source, S1.2, VCC1.-
  N3: U1.Pin_6, R1.Pin_0
  5V: U1.Pin_8, R3.Pin_0, Part1.5V, VCC1.+, Grove1.VCC
  N4: Q1.gate, R1.Pin_1
  GND: Q1.drain, Part1.GND, Part1.D5, Part1.D7, S2.Pin_1, S2.Pin_2, S4.Pin_1, S4.Pin_2, SP1.+, Grove1.GND
  N5: Part1.D6, S3.Pin_1, S3.Pin_2
  N6: Part1.D8, R4.Pin_0
  N7: Part1.A5, Grove1.SCL
  N8: Part1.A4, Grove1.SDA
  N9: S2.Pin_3, S2.Pin_4
  N10: S3.Pin_3, S3.Pin_4
  N11: S4.Pin_3, S4.Pin_4
  N12: SP1.-, R4.Pin_1

custom parts:
  Vertical Resistor: A generic resistor (0.25W)
