# Fritzing sketch ArduinoRelayShutoff (saved by Fritzing 0.9.3b)
stripboards: 1
breadboards: 1

parts:
  S1 = Momentary Switch [package=ksa_sealed_tac_switch]
  Part1 = Arduino Nano (Rev3.0)
  S2 = Pushbutton [package="[THT]"]
  S3 = Pushbutton [package="[THT]"]
  S4 = Pushbutton [package="[THT]"]
  SP1 = SPEAKER [package=pcb_mount_speaker]
  R4 = Resistor [tolerance=±5% resistance=1k package=THT]
  Grove1 = Grove OLED 128x96
  Part2 = songle relay
  VCC1 = Battery
  M1 = RioRand LM2596

nets:
  N1: S1.2, Part2.COMMON, M1.Pin_2
  N2: S1.4, Part2.NO, VCC1.-
  GND: Part1.GND, Part1.D5, Part1.D7, S2.Pin_1, S2.Pin_2, S4.Pin_1, S4.Pin_2, SP1.+, Grove1.GND, M1.Pin_4
  N3: Part1.D6, S3.Pin_1, S3.Pin_2
  N4: Part1.D8, R4.Pin_0
  VCC: Part1.5V, Grove1.VCC, Part2.VCC, M1.Pin_3
  N5: Part1.A5, Grove1.SCL
  N6: Part1.A4, Grove1.SDA
  N7: S2.Pin_3, S2.Pin_4
  N8: S3.Pin_3, S3.Pin_4
  N9: S4.Pin_3, S4.Pin_4
  N10: SP1.-, R4.Pin_1
